// Logisim project Lab1.2.circ as structural Verilog: 3 circuits, main circuit main
module main (
  input  x,
  input  y,
  input  z,
  output out_4
);

  wire and_1_out, and_2_out, not_1_out, not_2_out;

  not not_1 (not_1_out, y);
  not not_2 (not_2_out, x);
  and and_1 (and_1_out, x, not_1_out);
  and and_2 (and_2_out, not_2_out, z);
  or or_1 (out_4, and_1_out, and_2_out);

  // Notes on the sheet:
  //   Yêu cầu 1)
  //   x.y'
  //   x'.z
endmodule

module a (
  input  A,
  input  B,
  input  C,
  input  X,
  input  Y,
  input  Z,
  output out_7,
  output out_8
);

  wire and_1_out, and_2_out, and_3_out, and_4_out, and_5_out, or_1_out;

  and and_1 (and_1_out, A, B, C);
  and and_2 (and_2_out, A, B);
  and and_3 (and_3_out, A, B, C);
  and and_4 (and_4_out, X, Y);
  and and_5 (and_5_out, X, Y, Z);
  or or_1 (or_1_out, and_1_out, and_2_out);
  or or_2 (out_8, and_4_out, and_5_out);
  or or_3 (out_7, or_1_out, and_3_out);

  // Notes on the sheet:
  //   a)
  //   b)
endmodule

module b (
  input  X,
  input  Y,
  input  Z,
  output out_4
);

  wire and_1_out, and_2_out;

  and and_1 (and_1_out, X, Y);
  and and_2 (and_2_out, X, Y, Z);
  or or_1 (out_4, and_1_out, and_2_out);
endmodule
