// Logisim project Lab1_3.circ as structural Verilog
module _2__1_MUX (
  input  in_0,
  input  in_1,
  input  select,
  output out
);

  wire and_1_out, and_2_out, not_1_out;

  not not_1 (not_1_out, select);
  and and_1 (and_1_out, in_0, not_1_out);
  and and_2 (and_2_out, in_1, select);
  or or_1 (out, and_1_out, and_2_out);
endmodule

module _4__1_MUX (
  input  in_00,
  input  in01,
  input  in10,
  input  in11,
  input  sel0,
  input  set1,
  output out
);

  wire n2_1_mux_1_out, n2_1_mux_2_out;

  _2__1_MUX u_2_1_mux_1 (.in_0(in_00), .in_1(in01), .select(set1), .out(n2_1_mux_1_out));
  _2__1_MUX u_2_1_mux_2 (.in_0(in10), .in_1(in11), .select(set1), .out(n2_1_mux_2_out));
  _2__1_MUX u_2_1_mux_3 (.in_0(n2_1_mux_1_out), .in_1(n2_1_mux_2_out), .select(sel0), .out(out));
endmodule
