// Logisim project Lab2.circ as structural Verilog: 1 circuit, main circuit main
module main (
  input  [3:0] in_1
);

  LED led_1 (.in(in_1[3]));
  LED led_2 (.in(in_1[1]));
  LED led_3 (.in(in_1[2]));
  LED led_4 (.in(in_1[0]));
  Hex_Digit_Display hex_digit_display_1 (.value(in_1));  // open: dp
endmodule
