// Logisim project bai2.circ as structural Verilog: 6 circuits, main circuit Câu 1
module \Câu_1  (
  input  in_1,
  input  in_2,
  input  in_3,
  input  in_4,
  input  [3:0] in_5
);

  LED led_1 ();  // open: in
  LED led_2 ();  // open: in
  LED led_3 ();  // open: in
  Hex_Digit_Display hex_digit_display_1 (.value({in_1, in_2, in_3, in_4}));  // open: dp
  Hex_Digit_Display hex_digit_display_2 (.value(in_5));  // open: dp
  LED led_4 ();  // open: in
endmodule

module \Câu_2a  (
  input  a,
  input  in_2,
  output s,
  output c
);

  xor xor_1 (s, a, in_2);
  and and_1 (c, a, in_2);
endmodule

module \Câu_2b  (
  input  a,
  input  b
);

  wire \câu_2a_1_c , \câu_2a_1_s ;

  \Câu_2a  \câu_2a_1  (.a(a), .in_2(b), .s(\câu_2a_1_s ), .c(\câu_2a_1_c ));
  LED s (.in(\câu_2a_1_s ));
  LED c (.in(\câu_2a_1_c ));
endmodule

module \Câu_3  (
  input  a,
  input  b,
  output x,
  output y
);

  wire and_1_out, and_2_out, not_1_out, not_2_out, not_3_out;

  not not_1 (not_1_out, b);
  not not_2 (not_2_out, a);
  not not_3 (not_3_out, b);
  or or_1 (x, not_1_out, a);
  and and_1 (and_1_out, not_2_out, b);
  and and_2 (and_2_out, a, not_3_out);
  or or_2 (y, and_1_out, and_2_out);
endmodule

module \Câu_4  (
  input  a
);

  Clock Clock (.out(a));
  LED led_1 (.in(a));
  LED led_2 (.in(a));
  LED led_3 (.in(a));

  // Notes on the sheet:
  //   LED
endmodule

module \Câu_5  (
);

  wire clock_1_out;
  wire [2:0] counter_1_q, rom_1_data;

  Clock clock_1 (.out(clock_1_out));
  Counter #(.width(3), .max('h7), .trigger("falling")) counter_1 (
    .load(clock_1_out), .Q(counter_1_q), .clk(clock_1_out));  // open: D, count, carry, clr
  ROM #(.addrWidth(3), .dataWidth(3)) rom_1 (.addr(counter_1_q), .data(rom_1_data));  // open: sel
  LED led_1 (.in(rom_1_data[0]));
  LED led_2 (.in(rom_1_data[1]));
  LED led_3 (.in(rom_1_data[2]));

  // Notes on the sheet:
  //   contents of rom_1 (hex, n*v repeats v):
  //   1 1 4 4 2 2 1 1
  //   đèn đỏ
  //   đèn vàng
  //   đèn xanh
endmodule
