// Logisim project tuan4.circ as structural Verilog: 4 circuits, main circuit Traffic LED
module Traffic_LED (
);

  wire clock_1_out;
  wire [2:0] counter_1_q, rom_1_data;

  Clock clock_1 (.out(clock_1_out));
  Counter #(.width(3), .max('h7), .trigger("falling")) counter_1 (
    .load(clock_1_out), .Q(counter_1_q), .clk(clock_1_out));  // open: D, count, carry, clr
  ROM #(.addrWidth(3), .dataWidth(3)) rom_1 (.addr(counter_1_q), .data(rom_1_data));  // open: sel
  LED led_1 (.in(rom_1_data[0]));
  LED led_2 (.in(rom_1_data[1]));
  LED led_3 (.in(rom_1_data[2]));

  // Notes on the sheet:
  //   contents of rom_1 (hex, n*v repeats v):
  //   1 1 4 4 2 2 1 1
  //   đèn đỏ
  //   đèn vàng
  //   đèn xanh
endmodule

module Chuc_cac_ban_hoc_tot (
);

  wire button_1_out, clock_1_out;
  wire [6:0] counter_1_q, rom_1_data;

  Clock clock_1 (.out(clock_1_out));
  Counter #(.width(7), .max('h7f)) counter_1 (
    .Q(counter_1_q), .clk(clock_1_out), .clr(button_1_out));  // open: load, D, count, carry
  Button button_1 (.out(button_1_out));
  ROM #(.addrWidth(7), .dataWidth(7)) rom_1 (.addr(counter_1_q), .data(rom_1_data));  // open: sel
  TTY tty_1 (.data(rom_1_data), .clk(clock_1_out), .clr(button_1_out));  // open: we

  // Notes on the sheet:
  //   contents of rom_1 (hex, n*v repeats v):
  //   58 69 6e 20 63 68 61 6f 20 63 61 63 20 62 61 6e 21 a 43 68 75 63 20 63 61 63 20 62 61 6e 20 38 6f 63
  //   20 74 6f 74
endmodule

module \Đèn_LED  (
);

  wire clock_1_out;
  wire [3:0] counter_1_q, rom_1_data;

  Clock clock_1 (.out(clock_1_out));
  Counter #(.width(4), .max('hf), .trigger("falling")) counter_1 (
    .load(clock_1_out), .Q(counter_1_q), .clk(clock_1_out));  // open: D, count, carry, clr
  ROM #(.addrWidth(4), .dataWidth(4)) rom_1 (.addr(counter_1_q), .data(rom_1_data));  // open: sel
  Hex_Digit_Display hex_digit_display_1 (.value(rom_1_data));  // open: dp

  // Notes on the sheet:
  //   contents of rom_1 (hex, n*v repeats v):
  //   0 1 2 3 4 5 6 7 8 9 a b c d e f
endmodule

module \câu4  (
);

  wire button_1_out, clock_1_out, controlled_buffer_1_out, keyboard_1_avail;
  wire [6:0] keyboard_1_data;

  Clock clock_1 (.out(clock_1_out));
  Button button_1 (.out(button_1_out));
  assign controlled_buffer_1_out = keyboard_1_avail ? clock_1_out : 1'bz;  // Controlled_Buffer controlled_buffer_1
  Keyboard keyboard_1 (
    .clk(controlled_buffer_1_out), .avail(keyboard_1_avail), .data(keyboard_1_data));  // open: re, clr
  TTY tty_1 (.data(keyboard_1_data), .clk(clock_1_out), .clr(button_1_out));  // open: we
endmodule
